// Logisim project cpu.circ as structural Verilog: 9 circuits, main circuit main
module main (
  input  in_1
);

  wire and_1_out, and_2_out, beqz, blt, bran, clk, in_0, itype, jal, jr, jumps, keyboard_1_avail, lw,
       memory_latch_1_oe_latched, memory_latch_1_we_latched, nor_1_out, not_2_out, not_3_out, out_0, rTorD,
       sw, we;
  wire [2:0] ALUop, rd, read, rs_t, rt_t, shamt;
  wire [5:0] im;
  wire [7:0] kout;
  wire [11:0] address;
  wire [15:0] alu_4_outa, aluo, alurt, aout1, aout2, \do , ex_im, memory_latch_1_address_latched,
       memory_latch_1_data_in_latched, mout1, mout2, mout3, mout4, mout5, mout6, rom_1_data, rout, Rs, Rt;

  Keyboard #(.trigger("falling")) keyboard_1 (
    .clk(clk), .re(in_0), .clr(in_1), .avail(keyboard_1_avail), .data(kout[6:0]));
  Clock clock_1 (.out(clk));
  not not_1 (kout[7], keyboard_1_avail);
  not not_2 (not_2_out, clk);
  ROM #(.addrWidth(16), .dataWidth(16)) rom_1 (.addr(\do ), .data(rom_1_data));
  TTY #(.rows(13), .cols(80)) tty_1 (.data(Rs[6:0]), .clk(clk), .we(out_0), .clr(in_1));
  singleRegister singleregister_1 (.write_enable(1'b1), .clk(not_2_out), .reset(in_1), .dataIn(mout3), .dataout(\do ));
  Multiplexer #(.width(3), .enable("false")) multiplexer_1 (.in0(rd), .in1(rt_t), .out(read), .sel(rTorD));
  mydecoder mydecoder_1 (
    .in_1(rom_1_data), .junior(jr), .beqz(beqz), .lw(lw), .sw(sw), .blt(blt), .jal(jal), .data_input(in_0),
    .data_output(out_0), .write_enable(we), .rTorD(rTorD), .jumper(jumps), .I(itype), .ALUOpCode(ALUop),
    .shamt(shamt), .rd(rd), .rt(rt_t), .rs(rs_t), .immediate(im), .jaddy(address));
  RegisterFile registerfile_1 (
    .clk(clk), .ReadReg1(rs_t), .ReadReg2(rt_t), .reset(in_1), .rd(read), .writenable(we), .writeData(mout6),
    .rsval(Rs), .rtval(Rt));
  assign ex_im = {{10{im[5]}}, im};  // Bit_Extender bit_extender_1
  ALU alu_1 (.rs(\do ), .rt(16'h1), .shamt(3'b000), .aluop(3'b000), .outa(aout1));
  Multiplexer #(.width(16), .enable("false")) multiplexer_2 (.in0(Rt), .in1(ex_im), .out(alurt), .sel(itype));
  not not_3 (not_3_out, clk);
  ALU alu_2 (.rs(Rs), .rt(alurt), .shamt(shamt), .aluop(ALUop), .outa(aluo));
  ALU alu_3 (.rs(aout1), .rt(ex_im), .shamt(3'b000), .aluop(3'b000), .outa(aout2));
  memory_latch memory_latch_1 (
    .address(aluo), .WE(sw), .clk(not_3_out), .data_in(Rt), .address_latched(memory_latch_1_address_latched),
    .WE_latched(memory_latch_1_we_latched), .OE_latched(memory_latch_1_oe_latched),
    .data_in_latched(memory_latch_1_data_in_latched));
  nor nor_1 (nor_1_out, Rs[0], Rs[1], Rs[2], Rs[3], Rs[4], Rs[5], Rs[6], Rs[7], Rs[9], Rs[10], Rs[11], Rs[12], Rs[13], Rs[14], Rs[15], Rs[8]);
  Multiplexer #(.width(16), .enable("false")) multiplexer_3 (.in0(aout1), .in1(aout2), .out(mout1), .sel(bran));
  RAM #(.addrWidth(16), .dataWidth(16), .trigger("high"), .databus("bibus")) ram_1 (
    .addr(memory_latch_1_address_latched), .we(memory_latch_1_we_latched), .oe(memory_latch_1_oe_latched),
    .din(memory_latch_1_data_in_latched), .dout(rout));
  Multiplexer #(.width(16), .enable("false")) multiplexer_4 (
    .in0(mout1), .in1({4'b0000, address}), .out(mout2), .sel(jumps));
  and and_1 (and_1_out, nor_1_out, beqz);
  ALU alu_4 (.rs(Rs), .rt(Rt), .shamt(3'b001), .aluop(3'b001), .outa(alu_4_outa));
  and and_2 (and_2_out, blt, alu_4_outa[15]);
  Multiplexer #(.width(16), .enable("false")) multiplexer_5 (.in0(mout2), .in1(Rs), .out(mout3), .sel(jr));
  or or_1 (bran, and_1_out, and_2_out);
  Multiplexer #(.width(16), .enable("false")) multiplexer_6 (.in0(aluo), .in1(rout), .out(mout4), .sel(lw));
  Multiplexer #(.width(16), .enable("false")) multiplexer_7 (.in0(mout4), .in1(aout1), .out(mout5), .sel(jal));
  Multiplexer #(.width(16), .enable("false")) multiplexer_8 (
    .in0(mout5), .in1({{8{1'b0}}, kout}), .out(mout6), .sel(in_0));

  // Other names for the same wires on the sheet: jadd[11:0] = address; reset = in_1; rsOutput[6:0] = Rs[6:0]

  // Notes on the sheet:
  //   contents of rom_1 (hex, n*v repeats v):
  //   e00f e00f e00f
endmodule

module myShift (
  input  right,
  input  [15:0] input1,
  input  [2:0] shamt,
  output [15:0] shft
);

  wire [15:0] shl1, shl2, shl4, shr1, shr2, shr4;

  Multiplexer #(.width(16), .enable("false")) multiplexer_1 (.in0(shl4), .in1(shr4), .out(shft), .sel(right));
  Multiplexer #(.width(16), .enable("false")) multiplexer_2 (
    .in0(input1), .in1({input1[14:0], 1'b0}), .out(shl1), .sel(shamt[0]));
  Multiplexer #(.width(16), .enable("false")) multiplexer_3 (
    .in0(input1), .in1({1'b0, input1[15:1]}), .out(shr1), .sel(shamt[0]));
  Multiplexer #(.width(16), .enable("false")) multiplexer_4 (
    .in0(shl1), .in1({shl1[13:0], 2'b00}), .out(shl2), .sel(shamt[1]));
  Multiplexer #(.width(16), .enable("false")) multiplexer_5 (
    .in0(shr1), .in1({2'b00, shr1[15:2]}), .out(shr2), .sel(shamt[1]));
  Multiplexer #(.width(16), .enable("false")) multiplexer_6 (
    .in0(shl2), .in1({shl2[11:0], 4'b0000}), .out(shl4), .sel(shamt[2]));
  Multiplexer #(.width(16), .enable("false")) multiplexer_7 (
    .in0(shr2), .in1({4'b0000, shr2[15:4]}), .out(shr4), .sel(shamt[2]));

  // Other names for the same wires on the sheet: sh1 = shamt[0]; sh2 = shamt[1]; sh4 = shamt[2]
endmodule

module memory_latch (
  input  [15:0] address,
  input  WE,
  input  clk,
  input  [15:0] data_in,
  output [15:0] address_latched,
  output WE_latched,
  output OE_latched,
  output [15:0] data_in_latched
);

  wire DMwe_latch_q;
  wire [15:0] addr_latch_q;

  Register #(.width(16), .trigger("falling")) addr_latch (
    .D(address), .en(WE), .clk(clk), .Q(addr_latch_q));  // open: clr
  D_Flip_Flop #(.trigger("falling")) DMwe_latch (.D(WE), .clk(clk), .Q(DMwe_latch_q));  // open: Qn, preset, reset
  Register #(.width(16), .trigger("falling")) data_to_be_written (
    .D(data_in), .en(WE), .clk(clk), .Q(data_in_latched));  // open: clr
  Multiplexer #(.width(16), .enable("false")) multiplexer_1 (
    .in0(address), .in1(addr_latch_q), .out(address_latched), .sel(DMwe_latch_q));
  and and_1 (WE_latched, clk, DMwe_latch_q);
  not not_1 (OE_latched, WE_latched);
endmodule

module mydecoder (
  input  [15:0] in_1,
  output junior,
  output beqz,
  output lw,
  output sw,
  output blt,
  output jal,
  output data_input,
  output data_output,
  output write_enable,
  output rTorD,
  output jumper,
  output I,
  output [2:0] ALUOpCode,
  output [2:0] shamt,
  output [2:0] rd,
  output [2:0] rt,
  output [2:0] rs,
  output [5:0] immediate,
  output [11:0] jaddy
);

  wire add, addi, j, \not , sll, srl, sub, \xor ;

  Decoder #(.select(4), .enable("false")) decoder_1 (
    .out0(add), .out1(sub), .out2(addi), .out3(\not ), .out4(\xor ), .out5(sll), .out6(srl), .out7(lw),
    .out8(sw), .out9(beqz), .out10(blt), .out11(j), .out12(junior), .out13(jal), .out14(data_input),
    .out15(data_output), .sel(in_1[15:12]));
  or or_1 (ALUOpCode[2], \not , \xor );
  or or_2 (ALUOpCode[1], \xor , sll, srl);
  or or_3 (ALUOpCode[0], srl, sub);
  or or_4 (write_enable, add, addi, sub, \not , \xor , sll, srl, lw, jal, data_input);
  or or_5 (rTorD, addi, lw, sw, beqz, blt, junior, j, data_output);
  or or_6 (I, addi, sw, lw);
  or or_7 (jumper, j, jal);
  Multiplexer #(.width(3), .enable("false")) multiplexer_1 (.in0(in_1[5:3]), .in1(3'b111), .out(rd), .sel(jal));

  assign immediate = in_1[5:0];
  assign jaddy = in_1[11:0];
  assign rs = in_1[11:9];
  assign rt = in_1[8:6];
  assign shamt = in_1[2:0];

  // Other names for the same wires on the sheet: holder[11:0] = in_1[11:0]; input = data_input; jr = junior;
  //   opcode[3:0] = in_1[15:12]; output = data_output
endmodule

module myadder (
  input  [15:0] B,
  input  [15:0] A,
  input  sub,
  output ovf,
  output [15:0] res
);

  wire add_1bit_1_c2, add_1bit_2_c2, add_1bit_3_c2, add_1bit_4_c2, add_1bit_5_c2, add_1bit_6_c2,
       add_1bit_7_c2, add_1bit_8_c2, add_1bit_9_c2, add_1bit_10_c2, add_1bit_11_c2, add_1bit_12_c2,
       add_1bit_13_c2, add_1bit_14_c2, add_1bit_15_c2, add_1bit_16_c2, xor_2_out, xor_3_out, xor_4_out,
       xor_5_out, xor_6_out, xor_7_out, xor_8_out, xor_9_out, xor_10_out, xor_11_out, xor_12_out, xor_13_out,
       xor_14_out, xor_15_out, xor_16_out, xor_17_out;

  xor xor_1 (ovf, add_1bit_1_c2, add_1bit_2_c2);
  add_1bit add_1bit_1 (.C1(add_1bit_2_c2), .A(A[15]), .B(xor_2_out), .C2(add_1bit_1_c2), .num(res[15]));
  xor xor_2 (xor_2_out, B[15], sub);
  add_1bit add_1bit_2 (.C1(add_1bit_3_c2), .A(A[14]), .B(xor_3_out), .C2(add_1bit_2_c2), .num(res[14]));
  xor xor_3 (xor_3_out, B[14], sub);
  xor xor_4 (xor_4_out, B[13], sub);
  add_1bit add_1bit_3 (.C1(add_1bit_4_c2), .A(A[13]), .B(xor_4_out), .C2(add_1bit_3_c2), .num(res[13]));
  xor xor_5 (xor_5_out, B[12], sub);
  add_1bit add_1bit_4 (.C1(add_1bit_5_c2), .A(A[12]), .B(xor_5_out), .C2(add_1bit_4_c2), .num(res[12]));
  xor xor_6 (xor_6_out, B[11], sub);
  add_1bit add_1bit_5 (.C1(add_1bit_6_c2), .A(A[11]), .B(xor_6_out), .C2(add_1bit_5_c2), .num(res[11]));
  xor xor_7 (xor_7_out, B[10], sub);
  add_1bit add_1bit_6 (.C1(add_1bit_7_c2), .A(A[10]), .B(xor_7_out), .C2(add_1bit_6_c2), .num(res[10]));
  xor xor_8 (xor_8_out, B[9], sub);
  xor xor_9 (xor_9_out, B[8], sub);
  add_1bit add_1bit_7 (.C1(add_1bit_8_c2), .A(A[9]), .B(xor_8_out), .C2(add_1bit_7_c2), .num(res[9]));
  xor xor_10 (xor_10_out, B[7], sub);
  add_1bit add_1bit_8 (.C1(add_1bit_9_c2), .A(A[8]), .B(xor_9_out), .C2(add_1bit_8_c2), .num(res[8]));
  xor xor_11 (xor_11_out, B[6], sub);
  add_1bit add_1bit_9 (.C1(add_1bit_10_c2), .A(A[7]), .B(xor_10_out), .C2(add_1bit_9_c2), .num(res[7]));
  xor xor_12 (xor_12_out, B[5], sub);
  add_1bit add_1bit_10 (.C1(add_1bit_11_c2), .A(A[6]), .B(xor_11_out), .C2(add_1bit_10_c2), .num(res[6]));
  xor xor_13 (xor_13_out, B[4], sub);
  xor xor_14 (xor_14_out, B[3], sub);
  add_1bit add_1bit_11 (.C1(add_1bit_12_c2), .A(A[5]), .B(xor_12_out), .C2(add_1bit_11_c2), .num(res[5]));
  xor xor_15 (xor_15_out, B[2], sub);
  add_1bit add_1bit_12 (.C1(add_1bit_13_c2), .A(A[4]), .B(xor_13_out), .C2(add_1bit_12_c2), .num(res[4]));
  xor xor_16 (xor_16_out, B[1], sub);
  add_1bit add_1bit_13 (.C1(add_1bit_14_c2), .A(A[3]), .B(xor_14_out), .C2(add_1bit_13_c2), .num(res[3]));
  xor xor_17 (xor_17_out, B[0], sub);
  add_1bit add_1bit_14 (.C1(add_1bit_15_c2), .A(A[2]), .B(xor_15_out), .C2(add_1bit_14_c2), .num(res[2]));
  add_1bit add_1bit_15 (.C1(add_1bit_16_c2), .A(A[1]), .B(xor_16_out), .C2(add_1bit_15_c2), .num(res[1]));
  add_1bit add_1bit_16 (.C1(sub), .A(A[0]), .B(xor_17_out), .C2(add_1bit_16_c2), .num(res[0]));
endmodule

module add_1bit (
  input  C1,
  input  A,
  input  B,
  output C2,
  output num
);

  wire and_1_out, and_2_out, xor_1_out;

  xor xor_1 (xor_1_out, B, A);
  and and_1 (and_1_out, A, B);
  and and_2 (and_2_out, xor_1_out, C1);
  or or_1 (C2, and_1_out, and_2_out);
  xor xor_2 (num, C1, xor_1_out);
endmodule

module RegisterFile (
  input  clk,
  input  [2:0] ReadReg1,
  input  [2:0] ReadReg2,
  input  reset,
  input  [2:0] rd,
  input  writenable,
  input  [15:0] writeData,
  output [15:0] rsval,
  output [15:0] rtval
);

  wire a1, a2, a3, a4, a5, a6, a7, decoder_2_out0, decoder_2_out1, decoder_2_out2, decoder_2_out3,
       decoder_2_out4, decoder_2_out5, decoder_2_out6, decoder_2_out7, decoder_3_out0, decoder_3_out1,
       decoder_3_out2, decoder_3_out3, decoder_3_out4, decoder_3_out5, decoder_3_out6, decoder_3_out7, we1,
       we2, we3, we4, we5, we6, we7;
  wire [15:0] r0, r1, r2, r3, r4, r5, r6, r7;

  Decoder #(.select(3), .enable("false")) decoder_1 (
    .out1(a1), .out2(a2), .out3(a3), .out4(a4), .out5(a5), .out6(a6), .out7(a7), .sel(rd));  // open: out0
  // Probe on r0
  // Probe on r4
  // Probe on r1
  // Probe on r5
  // Probe on r2
  // Probe on r6
  singleRegister singleregister_1 (.write_enable(1'b0), .clk(clk), .reset(reset), .dataIn(writeData), .dataout(r0));
  singleRegister singleregister_2 (.write_enable(we2), .clk(clk), .reset(reset), .dataIn(writeData), .dataout(r2));
  singleRegister singleregister_3 (.write_enable(we4), .clk(clk), .reset(reset), .dataIn(writeData), .dataout(r4));
  singleRegister singleregister_4 (.write_enable(we6), .clk(clk), .reset(reset), .dataIn(writeData), .dataout(r6));
  // Probe on r3
  // Probe on r7
  and and_1 (we1, a1, writenable);
  and and_2 (we5, a5, writenable);
  and and_3 (we2, a2, writenable);
  and and_4 (we6, a6, writenable);
  singleRegister singleregister_5 (.write_enable(we1), .clk(clk), .reset(reset), .dataIn(writeData), .dataout(r1));
  singleRegister singleregister_6 (.write_enable(we3), .clk(clk), .reset(reset), .dataIn(writeData), .dataout(r3));
  singleRegister singleregister_7 (.write_enable(we5), .clk(clk), .reset(reset), .dataIn(writeData), .dataout(r5));
  singleRegister singleregister_8 (.write_enable(we7), .clk(clk), .reset(reset), .dataIn(writeData), .dataout(r7));
  and and_5 (we3, a3, writenable);
  and and_6 (we7, a7, writenable);
  and and_7 (we4, a4, writenable);
  Decoder #(.select(3), .enable("false")) decoder_2 (
    .out0(decoder_2_out0), .out1(decoder_2_out1), .out2(decoder_2_out2), .out3(decoder_2_out3),
    .out4(decoder_2_out4), .out5(decoder_2_out5), .out6(decoder_2_out6), .out7(decoder_2_out7), .sel(ReadReg1));
  Decoder #(.select(3), .enable("false")) decoder_3 (
    .out0(decoder_3_out0), .out1(decoder_3_out1), .out2(decoder_3_out2), .out3(decoder_3_out3),
    .out4(decoder_3_out4), .out5(decoder_3_out5), .out6(decoder_3_out6), .out7(decoder_3_out7), .sel(ReadReg2));
  assign rsval = decoder_2_out3 ? r3 : 16'bz;  // Controlled_Buffer controlled_buffer_1
  assign rsval = decoder_2_out2 ? r2 : 16'bz;  // Controlled_Buffer controlled_buffer_2
  assign rsval = decoder_2_out1 ? r1 : 16'bz;  // Controlled_Buffer controlled_buffer_3
  assign rsval = decoder_2_out0 ? r0 : 16'bz;  // Controlled_Buffer controlled_buffer_4
  assign rtval = decoder_3_out3 ? r3 : 16'bz;  // Controlled_Buffer controlled_buffer_5
  assign rtval = decoder_3_out2 ? r2 : 16'bz;  // Controlled_Buffer controlled_buffer_6
  assign rtval = decoder_3_out1 ? r1 : 16'bz;  // Controlled_Buffer controlled_buffer_7
  assign rtval = decoder_3_out0 ? r0 : 16'bz;  // Controlled_Buffer controlled_buffer_8
  assign rsval = decoder_2_out7 ? r7 : 16'bz;  // Controlled_Buffer controlled_buffer_9
  assign rsval = decoder_2_out6 ? r6 : 16'bz;  // Controlled_Buffer controlled_buffer_10
  assign rsval = decoder_2_out5 ? r5 : 16'bz;  // Controlled_Buffer controlled_buffer_11
  assign rsval = decoder_2_out4 ? r4 : 16'bz;  // Controlled_Buffer controlled_buffer_12
  assign rtval = decoder_3_out7 ? r7 : 16'bz;  // Controlled_Buffer controlled_buffer_13
  assign rtval = decoder_3_out6 ? r6 : 16'bz;  // Controlled_Buffer controlled_buffer_14
  assign rtval = decoder_3_out5 ? r5 : 16'bz;  // Controlled_Buffer controlled_buffer_15
  assign rtval = decoder_3_out4 ? r4 : 16'bz;  // Controlled_Buffer controlled_buffer_16
endmodule

module singleRegister (
  input  write_enable,
  input  clk,
  input  reset,
  input  [15:0] dataIn,
  output [15:0] dataout
);

  wire clk_t;

  and and_1 (clk_t, write_enable, clk);
  D_Flip_Flop d_ff_1 (.D(dataIn[0]), .clk(clk_t), .Q(dataout[0]), .reset(reset));  // open: Qn, preset
  D_Flip_Flop d_ff_2 (.D(dataIn[4]), .clk(clk_t), .Q(dataout[4]), .reset(reset));  // open: Qn, preset
  D_Flip_Flop d_ff_3 (.D(dataIn[8]), .clk(clk_t), .Q(dataout[8]), .reset(reset));  // open: Qn, preset
  D_Flip_Flop d_ff_4 (.D(dataIn[12]), .clk(clk_t), .Q(dataout[12]), .reset(reset));  // open: Qn, preset
  D_Flip_Flop d_ff_5 (.D(dataIn[1]), .clk(clk_t), .Q(dataout[1]), .reset(reset));  // open: Qn, preset
  D_Flip_Flop d_ff_6 (.D(dataIn[5]), .clk(clk_t), .Q(dataout[5]), .reset(reset));  // open: Qn, preset
  D_Flip_Flop d_ff_7 (.D(dataIn[9]), .clk(clk_t), .Q(dataout[9]), .reset(reset));  // open: Qn, preset
  D_Flip_Flop d_ff_8 (.D(dataIn[13]), .clk(clk_t), .Q(dataout[13]), .reset(reset));  // open: Qn, preset
  D_Flip_Flop d_ff_9 (.D(dataIn[2]), .clk(clk_t), .Q(dataout[2]), .reset(reset));  // open: Qn, preset
  D_Flip_Flop d_ff_10 (.D(dataIn[6]), .clk(clk_t), .Q(dataout[6]), .reset(reset));  // open: Qn, preset
  D_Flip_Flop d_ff_11 (.D(dataIn[10]), .clk(clk_t), .Q(dataout[10]), .reset(reset));  // open: Qn, preset
  D_Flip_Flop d_ff_12 (.D(dataIn[14]), .clk(clk_t), .Q(dataout[14]), .reset(reset));  // open: Qn, preset
  D_Flip_Flop d_ff_13 (.D(dataIn[3]), .clk(clk_t), .Q(dataout[3]), .reset(reset));  // open: Qn, preset
  D_Flip_Flop d_ff_14 (.D(dataIn[7]), .clk(clk_t), .Q(dataout[7]), .reset(reset));  // open: Qn, preset
  D_Flip_Flop d_ff_15 (.D(dataIn[11]), .clk(clk_t), .Q(dataout[11]), .reset(reset));  // open: Qn, preset
  D_Flip_Flop d_ff_16 (.D(dataIn[15]), .clk(clk_t), .Q(dataout[15]), .reset(reset));  // open: Qn, preset

  // Other names for the same wires on the sheet: in0 = dataIn[0]; in1 = dataIn[1]; in2 = dataIn[2]; in3 = dataIn[3];
  //   in4 = dataIn[4]; in5 = dataIn[5]; in6 = dataIn[6]; in7 = dataIn[7]; in8 = dataIn[8]; in9 = dataIn[9];
  //   in10 = dataIn[10]; in11 = dataIn[11]; in12 = dataIn[12]; in13 = dataIn[13]; in14 = dataIn[14];
  //   in15 = dataIn[15]; out0 = dataout[0]; out1 = dataout[1]; out2 = dataout[2]; out3 = dataout[3];
  //   out4 = dataout[4]; out5 = dataout[5]; out6 = dataout[6]; out7 = dataout[7]; out8 = dataout[8];
  //   out9 = dataout[9]; out10 = dataout[10]; out11 = dataout[11]; out12 = dataout[12]; out13 = dataout[13];
  //   out14 = dataout[14]; out15 = dataout[15]
endmodule

module ALU (
  input  [15:0] rs,
  input  [15:0] rt,
  input  [2:0] shamt,
  input  [2:0] aluop,
  output [15:0] outa
);

  wire [15:0] multiplexer_1_out, multiplexer_2_out, myadder_1_res, myshift_1_shft, not_1_out, xor_1_out;

  assign not_1_out = ~rs;  // NOT_Gate not_1, 16 bits wide
  assign xor_1_out = rs ^ rt;  // XOR_Gate xor_1, 16 bits wide
  myShift myshift_1 (.right(aluop[0]), .input1(rs), .shamt(shamt), .shft(myshift_1_shft));
  myadder myadder_1 (.B(rt), .A(rs), .sub(aluop[0]), .res(myadder_1_res));  // open: ovf
  Multiplexer #(.width(16), .enable("false")) multiplexer_1 (
    .in0(myadder_1_res), .in1(myshift_1_shft), .out(multiplexer_1_out), .sel(aluop[1]));
  Multiplexer #(.width(16), .enable("false")) multiplexer_2 (
    .in0(not_1_out), .in1(xor_1_out), .out(multiplexer_2_out), .sel(aluop[1]));
  Multiplexer #(.width(16), .enable("false")) multiplexer_3 (
    .in0(multiplexer_1_out), .in1(multiplexer_2_out), .out(outa), .sel(aluop[2]));

  // Other names for the same wires on the sheet: in1[15:0] = rs; in2[15:0] = rt
endmodule
