// Logisim project my_adder.circ as structural Verilog: 2 circuits, main circuit main
module main (
  input  [15:0] B,
  input  [15:0] A,
  input  sub,
  output ovf,
  output [15:0] result
);

  wire add_1bit_1_c2, add_1bit_2_c2, add_1bit_3_c2, add_1bit_4_c2, add_1bit_5_c2, add_1bit_6_c2,
       add_1bit_7_c2, add_1bit_8_c2, add_1bit_9_c2, add_1bit_10_c2, add_1bit_11_c2, add_1bit_12_c2,
       add_1bit_13_c2, add_1bit_14_c2, add_1bit_15_c2, add_1bit_16_c2, xor_2_out, xor_3_out, xor_4_out,
       xor_5_out, xor_6_out, xor_7_out, xor_8_out, xor_9_out, xor_10_out, xor_11_out, xor_12_out, xor_13_out,
       xor_14_out, xor_15_out, xor_16_out, xor_17_out;

  xor xor_1 (ovf, add_1bit_1_c2, add_1bit_2_c2);
  add_1bit add_1bit_1 (.C1(add_1bit_2_c2), .A(A[15]), .B(xor_2_out), .C2(add_1bit_1_c2), .num(result[15]));
  xor xor_2 (xor_2_out, B[15], sub);
  add_1bit add_1bit_2 (.C1(add_1bit_3_c2), .A(A[14]), .B(xor_3_out), .C2(add_1bit_2_c2), .num(result[14]));
  xor xor_3 (xor_3_out, B[14], sub);
  add_1bit add_1bit_3 (.C1(add_1bit_4_c2), .A(A[13]), .B(xor_4_out), .C2(add_1bit_3_c2), .num(result[13]));
  xor xor_4 (xor_4_out, B[13], sub);
  xor xor_5 (xor_5_out, B[12], sub);
  add_1bit add_1bit_4 (.C1(add_1bit_5_c2), .A(A[12]), .B(xor_5_out), .C2(add_1bit_4_c2), .num(result[12]));
  xor xor_6 (xor_6_out, B[11], sub);
  add_1bit add_1bit_5 (.C1(add_1bit_6_c2), .A(A[11]), .B(xor_6_out), .C2(add_1bit_5_c2), .num(result[11]));
  xor xor_7 (xor_7_out, B[10], sub);
  add_1bit add_1bit_6 (.C1(add_1bit_7_c2), .A(A[10]), .B(xor_7_out), .C2(add_1bit_6_c2), .num(result[10]));
  xor xor_8 (xor_8_out, B[9], sub);
  add_1bit add_1bit_7 (.C1(add_1bit_8_c2), .A(A[9]), .B(xor_8_out), .C2(add_1bit_7_c2), .num(result[9]));
  xor xor_9 (xor_9_out, B[8], sub);
  xor xor_10 (xor_10_out, B[7], sub);
  add_1bit add_1bit_8 (.C1(add_1bit_9_c2), .A(A[8]), .B(xor_9_out), .C2(add_1bit_8_c2), .num(result[8]));
  xor xor_11 (xor_11_out, B[6], sub);
  add_1bit add_1bit_9 (.C1(add_1bit_10_c2), .A(A[7]), .B(xor_10_out), .C2(add_1bit_9_c2), .num(result[7]));
  xor xor_12 (xor_12_out, B[5], sub);
  add_1bit add_1bit_10 (.C1(add_1bit_11_c2), .A(A[6]), .B(xor_11_out), .C2(add_1bit_10_c2), .num(result[6]));
  xor xor_13 (xor_13_out, B[4], sub);
  add_1bit add_1bit_11 (.C1(add_1bit_12_c2), .A(A[5]), .B(xor_12_out), .C2(add_1bit_11_c2), .num(result[5]));
  xor xor_14 (xor_14_out, B[3], sub);
  xor xor_15 (xor_15_out, B[2], sub);
  add_1bit add_1bit_12 (.C1(add_1bit_13_c2), .A(A[4]), .B(xor_13_out), .C2(add_1bit_12_c2), .num(result[4]));
  xor xor_16 (xor_16_out, B[1], sub);
  add_1bit add_1bit_13 (.C1(add_1bit_14_c2), .A(A[3]), .B(xor_14_out), .C2(add_1bit_13_c2), .num(result[3]));
  xor xor_17 (xor_17_out, B[0], sub);
  add_1bit add_1bit_14 (.C1(add_1bit_15_c2), .A(A[2]), .B(xor_15_out), .C2(add_1bit_14_c2), .num(result[2]));
  add_1bit add_1bit_15 (.C1(add_1bit_16_c2), .A(A[1]), .B(xor_16_out), .C2(add_1bit_15_c2), .num(result[1]));
  add_1bit add_1bit_16 (.C1(sub), .A(A[0]), .B(xor_17_out), .C2(add_1bit_16_c2), .num(result[0]));
endmodule

module add_1bit (
  input  C1,
  input  A,
  input  B,
  output C2,
  output num
);

  wire and_1_out, and_2_out, xor_1_out;

  xor xor_1 (xor_1_out, B, A);
  and and_1 (and_1_out, A, B);
  and and_2 (and_2_out, xor_1_out, C1);
  or or_1 (C2, and_1_out, and_2_out);
  xor xor_2 (num, C1, xor_1_out);
endmodule
