// Logisim project robot.circ as structural Verilog: 1 circuit, main circuit main
module main (
  input  in_stopall,
  input  in_stopupdown,
  output out_tired,
  output out_1D,
  output out_2D
);

  wire and_1_out, and_2_out, and_3_out, and_4_out, and_5_out, and_6_out, and_7_out, and_8_out, and_9_out,
       clock_1_out, D0_q, D1_q, D2_q, not_1_out, not_2_out, not_3_out, not_4_out, not_5_out, not_6_out,
       not_7_out, not_8_out, not_9_out, not_10_out, not_11_out, not_12_out, not_13_out, not_14_out,
       not_15_out, not_16_out, not_17_out, not_18_out, not_19_out, not_20_out, or_2_out, or_3_out, or_5_out,
       or_6_out, or_8_out, or_9_out;

  not not_1 (not_1_out, D1_q);
  and and_1 (and_1_out, D2_q, not_1_out, D0_q);
  not not_2 (not_2_out, D0_q);
  and and_2 (and_2_out, D2_q, D1_q, not_2_out);
  or or_1 (out_tired, and_1_out, and_2_out);
  not not_3 (not_3_out, in_stopall);
  not not_4 (not_4_out, D2_q);
  or or_2 (or_2_out, D0_q, D1_q, not_4_out);
  and and_3 (and_3_out, not_3_out, in_stopupdown, or_2_out, or_3_out);
  D_Flip_Flop D0 (.D(and_3_out), .clk(clock_1_out), .Q(D0_q));  // open: Qn, preset, reset
  not not_5 (not_5_out, D0_q);
  not not_6 (not_6_out, D1_q);
  or or_3 (or_3_out, not_5_out, not_6_out);
  not not_7 (not_7_out, D2_q);
  not not_8 (not_8_out, D1_q);
  and and_4 (and_4_out, not_7_out, not_8_out, D0_q);
  or or_4 (out_1D, and_4_out, and_5_out);
  not not_9 (not_9_out, D1_q);
  and and_5 (and_5_out, D2_q, not_9_out, D0_q);
  not not_10 (not_10_out, in_stopall);
  not not_11 (not_11_out, in_stopupdown);
  and and_6 (and_6_out, not_11_out, not_10_out, or_5_out, or_6_out);
  not not_12 (not_12_out, D2_q);
  or or_5 (or_5_out, D0_q, D1_q, not_12_out);
  not not_13 (not_13_out, D0_q);
  not not_14 (not_14_out, D1_q);
  or or_6 (or_6_out, not_13_out, not_14_out);
  D_Flip_Flop D1 (.D(and_6_out), .clk(clock_1_out), .Q(D1_q));  // open: Qn, preset, reset
  not not_15 (not_15_out, D0_q);
  and and_7 (and_7_out, D2_q, D1_q, not_15_out);
  or or_7 (out_2D, and_7_out, and_8_out);
  not not_16 (not_16_out, D0_q);
  not not_17 (not_17_out, D2_q);
  and and_8 (and_8_out, not_17_out, D1_q, not_16_out);
  or or_8 (or_8_out, D0_q, D1_q);
  not not_18 (not_18_out, in_stopall);
  and and_9 (and_9_out, not_18_out, or_8_out, or_9_out);
  Clock clock_1 (.out(clock_1_out));
  not not_19 (not_19_out, D0_q);
  not not_20 (not_20_out, D1_q);
  or or_9 (or_9_out, not_19_out, not_20_out);
  D_Flip_Flop D2 (.D(and_9_out), .clk(clock_1_out), .Q(D2_q));  // open: Qn, preset, reset
endmodule
